// Logisim project ep4.circ as structural Verilog: 5 circuits, main circuit main
module main (
  input  [15:0] In,
  output [15:0] Out
);

  wire ALU, cl, clock_2_out, Cond, condicionais_1_cond__1_if_true, controlador_1_condbit,
       controlador_1_inn__31, controlador_1_lda__11, controlador_1_nop__50, controlador_1_sta__12, JMP,
       not_1_out, or_1_out, or_2_out, or_3_out, or_4_out, or_5_out, PRN, STP;
  wire [2:0] controlador_1_cond, controlador_1_conta;
  wire [7:0] \Endereço , multiplexer_2_out, pc_program_counter_1_saida, register_1_q;
  wire [15:0] ACC, alu_1_resultado, demultiplexer_1_out0, demultiplexer_1_out1, demultiplexer_2_out0,
       demultiplexer_2_out1, demultiplexer_3_out1, multiplexer_1_out, multiplexer_3_out, ram_1_data,
       register_3_q;

  Clock clock_1 (.out(cl));
  or or_1 (or_1_out, JMP, Cond);
  Clock #(.highDuration(2), .lowDuration(2)) clock_2 (.out(clock_2_out));
  // Probe on In
  PC__Program_Counter pc_program_counter_1 (
    .JMP(or_1_out), .STP(STP), .Saida(pc_program_counter_1_saida), .\Endereço (\Endereço ),
    .Clock(clock_2_out));
  Multiplexer #(.width(16), .enable("false")) multiplexer_1 (
    .in0(ACC), .in1(In), .out(multiplexer_1_out), .sel(controlador_1_inn__31));
  or or_2 (or_2_out, controlador_1_sta__12, controlador_1_inn__31, ALU, PRN, controlador_1_lda__11);
  Multiplexer #(.width(8), .enable("false")) multiplexer_2 (
    .in0(pc_program_counter_1_saida), .in1(\Endereço ), .out(multiplexer_2_out), .sel(or_2_out));
  or or_3 (or_3_out, controlador_1_sta__12, controlador_1_inn__31);
  RAM #(.dataWidth(16), .bus("separate")) ram_1 (
    .addr(multiplexer_2_out), .din(multiplexer_1_out), .data(ram_1_data), .str(or_3_out), .clk(cl));  // open: sel, ld, clr
  Demultiplexer #(.width(16), .enable("false")) demultiplexer_1 (
    .out0(demultiplexer_1_out0), .out1(demultiplexer_1_out1), .in(ram_1_data), .sel(or_4_out));
  or or_4 (or_4_out, controlador_1_lda__11, PRN, ALU);
  LED NOP (.in(controlador_1_nop__50));
  // Probe on register_1_q
  Controlador controlador_1 (
    .\Instrução (register_1_q), .LDA__11(controlador_1_lda__11), .STA__12(controlador_1_sta__12),
    .INN__31(controlador_1_inn__31), .PRN__41(PRN), .NOP__50(controlador_1_nop__50), .JMP__51(JMP),
    .STP__70(STP), .Conta(controlador_1_conta), .Cond(controlador_1_cond), .ContaBit(ALU),
    .CondBit(controlador_1_condbit));
  Register #(.width(16)) register_1 (
    .D(demultiplexer_1_out0), .Q({register_1_q, \Endereço }), .clk(cl));  // open: en, clr
  and and_1 (Cond, controlador_1_condbit, condicionais_1_cond__1_if_true);
  // Probe on \Endereço 
  Condicionais condicionais_1 (.Cond__1_if_true(condicionais_1_cond__1_if_true), .ACC(ACC), .Cond(controlador_1_cond));
  // Probe on controlador_1_conta
  not not_1 (not_1_out, PRN);
  Demultiplexer #(.width(16), .enable("false")) demultiplexer_2 (
    .out0(demultiplexer_2_out0), .out1(demultiplexer_2_out1), .in(demultiplexer_1_out1), .sel(not_1_out));
  // Probe on alu_1_resultado
  ALU alu_1 (
    .ACC(demultiplexer_3_out1), .XY(demultiplexer_1_out1), .\Operaçao (controlador_1_conta),
    .Resultado(alu_1_resultado));  // open: Overflow
  // Probe on demultiplexer_2_out1
  Multiplexer #(.width(16), .enable("false")) multiplexer_3 (
    .in0(demultiplexer_2_out1), .in1(alu_1_resultado), .out(multiplexer_3_out), .sel(ALU));
  or or_5 (or_5_out, ALU, controlador_1_lda__11);
  Register #(.width(16), .trigger("falling")) register_2 (
    .D(demultiplexer_2_out0), .en(PRN), .Q(Out), .clk(cl));  // open: clr
  // Probe on Out
  Register #(.width(16), .trigger("falling")) register_3 (
    .D(multiplexer_3_out), .en(or_5_out), .Q(register_3_q), .clk(cl));  // open: clr
  Demultiplexer #(.width(16), .enable("false")) demultiplexer_3 (
    .out0(ACC), .out1(demultiplexer_3_out1), .in(register_3_q), .sel(ALU));

  // Notes on the sheet:
  //   > Daniel Toshio Iwamoto      - nº USP: 8516782
  //   > Gustavo Chicato Wandeur - nº USP: 7557797
  //   > Leonardo Pereira Macedo - nº USP: 8536065
  //   PC (Program Counter)
  //   Componentes do grupo:
  //   EP4 - Algebra Booleana
  //   Professor: Junior Barrera
  //   Memória
  //   IR (Instruction Register)
  //   Acumulador
endmodule

// PC
module PC__Program_Counter (
  input  [7:0] \Endereço ,
  input  JMP,
  input  STP,
  input  Clock,
  output [7:0] Saida
);

  wire d_ff_1_qn, not_1_out, xor_1_out;

  D_Flip_Flop d_ff_1 (.clk(Clock), .Qn(d_ff_1_qn));  // open: D, Q, preset, en, reset
  not not_1 (not_1_out, Clock);
  ExactlyOne xor_1 (.out(xor_1_out), .in0(JMP), .in1(STP), .in2(d_ff_1_qn));
  Counter counter_1 (.load(JMP), .D(\Endereço ), .count(xor_1_out), .Q(Saida), .clk(not_1_out));  // open: carry, clr
endmodule

module Controlador (
  input  [7:0] \Instrução ,
  output LDA__11,
  output STA__12,
  output INN__31,
  output PRN__41,
  output NOP__50,
  output JMP__51,
  output STP__70,
  output ContaBit,
  output CondBit,
  output [2:0] Conta,
  output [2:0] Cond
);

  wire _0_L, _1_L, _1_R, _2_L, _2_R, _3_L, _3_R, _4_L, _4_R, _5_R, _6_R, _7_R, _8_R, _9_R, B_R, C_R, F_R,
       or_1_out, or_2_out;
  wire [2:0] bit_extender_1_out, bit_extender_2_out;
  wire [7:0] subtractor_1_out, subtractor_2_out;

  and and_1 (LDA__11, _0_L, B_R);
  Decoder #(.select(4), .enable("false")) decoder_1 (
    .out0(_0_L), .out1(_1_L), .out2(_2_L), .out3(_3_L), .out4(_4_L), .sel(\Instrução [7:4]));  // open: out5, out6, out7, out8, out9, out10, out11, out12, out13, out14, out15
  Bit_Extender #(.out_width(3)) bit_extender_1 (.in(subtractor_1_out), .out(bit_extender_1_out));
  Subtractor subtractor_1 (.a(\Instrução ), .b(8'h15), .out(subtractor_1_out));  // open: bin, bout
  and and_2 (STA__12, _0_L, C_R);
  and and_3 (ContaBit, _1_L, or_1_out);
  Multiplexer #(.width(3), .enable("false")) multiplexer_1 (
    .in0(3'b000), .in1(bit_extender_1_out), .out(Conta), .sel(ContaBit));
  and and_4 (INN__31, _1_L, F_R);
  or or_1 (or_1_out, _5_R, _6_R, _7_R, _8_R, _9_R);
  and and_5 (PRN__41, _2_L, _9_R);
  Decoder #(.select(4), .enable("false")) decoder_2 (
    .out1(_1_R), .out2(_2_R), .out3(_3_R), .out4(_4_R), .out5(_5_R), .out6(_6_R), .out7(_7_R), .out8(_8_R),
    .out9(_9_R), .out11(B_R), .out12(C_R), .out15(F_R), .sel(\Instrução [3:0]));  // open: out0, out10, out13, out14
  and and_6 (NOP__50, _3_L, _2_R);
  Subtractor subtractor_2 (.a(\Instrução ), .b(8'h34), .out(subtractor_2_out));  // open: bin, bout
  and and_7 (JMP__51, _3_L, _3_R);
  and and_8 (CondBit, _3_L, or_2_out);
  Bit_Extender #(.out_width(3)) bit_extender_2 (.in(subtractor_2_out), .out(bit_extender_2_out));
  and and_9 (STP__70, _4_L, _6_R);
  or or_2 (or_2_out, _2_R, _3_R, _4_R, _5_R, _6_R, _7_R);
  Multiplexer #(.width(3), .enable("false")) multiplexer_2 (
    .in0(3'b000), .in1(bit_extender_2_out), .out(Cond), .sel(CondBit));

  // Other names for the same wires on the sheet: Instruçao[7:0] = \Instrução 

  // Notes on the sheet:
  //   4 bits mais significativos
  //   Análise da instrução
  //   4 bits menos significativos
endmodule

module ALU (
  input  [15:0] ACC,
  input  [15:0] XY,
  input  [2:0] \Operaçao ,
  output [15:0] Resultado,
  output Overflow
);

  wire DivZero, Overflow_t, subtractor_1_bout;
  wire [15:0] \Adiçao , \Multiplicaçao , Quociente, Resto, \Subtraçao ;

  Adder #(.width(16)) adder_1 (.a(ACC), .b(XY), .out(\Adiçao ));  // open: cin, cout
  Multiplier #(.width(16)) multiplier_1 (.a(ACC), .b(XY), .out(\Multiplicaçao ));  // open: cin, cout
  Divider #(.width(16)) divider_1 (.a(ACC), .b(XY), .out(Quociente), .rem(Resto));  // open: upper
  // Probe on ACC
  // Probe on \Subtraçao 
  Subtractor #(.width(16)) subtractor_1 (.a(ACC), .b(XY), .out(\Subtraçao ), .bout(subtractor_1_bout));  // open: bin
  // Probe on subtractor_1_bout
  // Probe on XY
  or or_1 (Overflow, DivZero, Overflow_t);
  // Probe on Resultado
  Multiplexer #(.select(3), .width(16), .enable("false")) multiplexer_1 (
    .in0(\Adiçao ), .in1(\Subtraçao ), .in2(\Multiplicaçao ), .in3(Quociente), .in4(Resto), .out(Resultado),
    .sel(\Operaçao ));  // open: in5, in6, in7
endmodule

module Condicionais (
  input  [2:0] Cond,
  input  [15:0] ACC,
  output Cond__1_if_true
);

  wire comparator_1_eq, comparator_1_lt, comparator_2_eq, comparator_6_eq, comparator_6_gt, JDZ, JEQ, JGE,
       JGT, JLE, JLT;

  Comparator #(.width(16)) comparator_1 (
    .a(ACC), .b({16{1'b0}}), .eq(comparator_1_eq), .lt(comparator_1_lt));  // open: gt
  Comparator #(.width(16)) comparator_2 (.a(ACC), .b({16{1'b0}}), .eq(comparator_2_eq));  // open: gt, lt
  not not_1 (JDZ, comparator_2_eq);
  Comparator #(.width(16)) comparator_3 (.a(ACC), .b({16{1'b0}}), .gt(JGT));  // open: eq, lt
  Comparator #(.width(16)) comparator_4 (.a(ACC), .b({16{1'b0}}), .eq(JEQ));  // open: gt, lt
  Comparator #(.width(16)) comparator_5 (.a(ACC), .b({16{1'b0}}), .lt(JLT));  // open: gt, eq
  Comparator #(.width(16)) comparator_6 (
    .a(ACC), .b({16{1'b0}}), .gt(comparator_6_gt), .eq(comparator_6_eq));  // open: lt
  or or_1 (JLE, comparator_1_eq, comparator_1_lt);
  or or_2 (JGE, comparator_6_gt, comparator_6_eq);
  Multiplexer #(.select(3), .enable("false")) multiplexer_1 (
    .in0(JLE), .in1(JDZ), .in2(JGT), .in3(JEQ), .in4(JLT), .in5(JGE), .out(Cond__1_if_true), .sel(Cond));  // open: in6, in7
endmodule
